// Logisim project hac_02.circ as structural Verilog: 3 circuits, main circuit main
module main (
  input  [15:0] A,
  input  [15:0] B,
  output [15:0] Y,
  output OVF
);

  add16 add16_1 (.B16(B), .A16(A), .OVF(OVF), .Y16(Y));
endmodule

module add (
  input  A,
  input  B,
  input  C_IN,
  output Y,
  output C_OUT
);

  wire and_1_out, and_2_out, xor_1_out;

  xor xor_1 (xor_1_out, A, B);
  and and_1 (and_1_out, A, B);
  xor xor_2 (Y, xor_1_out, C_IN);
  and and_2 (and_2_out, C_IN, xor_1_out);
  or or_1 (C_OUT, and_2_out, and_1_out);
endmodule

module add16 (
  input  [15:0] A16,
  input  [15:0] B16,
  output OVF,
  output [15:0] Y16
);

  wire add_2_c_out, add_3_c_out, add_4_c_out, add_5_c_out, add_6_c_out, add_7_c_out, add_8_c_out,
       add_9_c_out, add_10_c_out, add_11_c_out, add_12_c_out, add_13_c_out, add_14_c_out, add_15_c_out,
       add_16_c_out;

  add add_1 (.A(A16[15]), .B(B16[15]), .C_IN(add_2_c_out), .Y(Y16[15]), .C_OUT(OVF));
  add add_2 (.A(A16[14]), .B(B16[14]), .C_IN(add_3_c_out), .Y(Y16[14]), .C_OUT(add_2_c_out));
  add add_3 (.A(A16[13]), .B(B16[13]), .C_IN(add_4_c_out), .Y(Y16[13]), .C_OUT(add_3_c_out));
  add add_4 (.A(A16[12]), .B(B16[12]), .C_IN(add_5_c_out), .Y(Y16[12]), .C_OUT(add_4_c_out));
  add add_5 (.A(A16[11]), .B(B16[11]), .C_IN(add_6_c_out), .Y(Y16[11]), .C_OUT(add_5_c_out));
  add add_6 (.A(A16[10]), .B(B16[10]), .C_IN(add_7_c_out), .Y(Y16[10]), .C_OUT(add_6_c_out));
  add add_7 (.A(A16[9]), .B(B16[9]), .C_IN(add_8_c_out), .Y(Y16[9]), .C_OUT(add_7_c_out));
  add add_8 (.A(A16[8]), .B(B16[8]), .C_IN(add_9_c_out), .Y(Y16[8]), .C_OUT(add_8_c_out));
  add add_9 (.A(A16[7]), .B(B16[7]), .C_IN(add_10_c_out), .Y(Y16[7]), .C_OUT(add_9_c_out));
  add add_10 (.A(A16[6]), .B(B16[6]), .C_IN(add_11_c_out), .Y(Y16[6]), .C_OUT(add_10_c_out));
  add add_11 (.A(A16[5]), .B(B16[5]), .C_IN(add_12_c_out), .Y(Y16[5]), .C_OUT(add_11_c_out));
  add add_12 (.A(A16[4]), .B(B16[4]), .C_IN(add_13_c_out), .Y(Y16[4]), .C_OUT(add_12_c_out));
  add add_13 (.A(A16[3]), .B(B16[3]), .C_IN(add_14_c_out), .Y(Y16[3]), .C_OUT(add_13_c_out));
  add add_14 (.A(A16[2]), .B(B16[2]), .C_IN(add_15_c_out), .Y(Y16[2]), .C_OUT(add_14_c_out));
  add add_15 (.A(A16[1]), .B(B16[1]), .C_IN(add_16_c_out), .Y(Y16[1]), .C_OUT(add_15_c_out));
  add add_16 (.A(A16[0]), .B(B16[0]), .C_IN(1'b0), .Y(Y16[0]), .C_OUT(add_16_c_out));
endmodule
